// Logisim project LC3.circ as structural Verilog: 19 circuits, main circuit main
module main (
);

  wire ADDR1MUX, ben_1_o, bit_5_1_o, CLK, GateALU, GateMARMUX, GateMDR, GatePC, LD_BEN, LD_CC, LD_IR, LD_MAR,
       LD_MDR, LD_PC, LD_REG, logic_1_n, logic_1_p, logic_1_z, MARMUX, MIO_EN, N_q, P_q, R_W, RST, Z_q;
  wire [1:0] ADDR2MUX, ALUK, DRMUX, PCMUX, SR1MUX;
  wire [2:0] dr_sel_1_out_3, sr1_sel_1_o, sr2_sel_1_o;
  wire [15:0] adder_1_out, adder_2_out, alu_1_res, controlled_buffer_1_out, IR, MAR, MDR, multiplexer_1_out,
       multiplexer_2_out, multiplexer_3_out, multiplexer_4_out, multiplexer_5_out, multiplexer_6_out, PC, R0,
       R1, R2, R3, R4, R5, R6, R7, ram_1_dout, register_file_1_sr1_out, register_file_1_sr2_out,
       sext4_0_1_out_2, sext5_0_1_out_2, sext8_0_1_out_2, sext10_0_1_out_2, zext7_0_1_out_2;

  assign controlled_buffer_1_out = GateMARMUX ? multiplexer_1_out : 16'bz;  // Controlled_Buffer controlled_buffer_1
  Multiplexer #(.width(16)) multiplexer_1 (
    .in0(zext7_0_1_out_2), .in1(adder_1_out), .out(multiplexer_1_out), .sel(MARMUX));
  ZEXT7_0 zext7_0_1 (.in_1(IR), .out_2(zext7_0_1_out_2));
  SEXT5_0 sext5_0_1 (.in_1(IR), .out_2(sext5_0_1_out_2));
  SEXT8_0 sext8_0_1 (.in_1(IR), .out_2(sext8_0_1_out_2));
  SEXT10_0 sext10_0_1 (.in_1(IR), .out_2(sext10_0_1_out_2));
  Multiplexer #(.width(16)) multiplexer_2 (
    .in0(controlled_buffer_1_out), .in1(ram_1_dout), .out(multiplexer_2_out), .sel(MIO_EN));
  Multiplexer #(.select(2), .width(16)) multiplexer_3 (
    .in0(adder_2_out), .in1(adder_1_out), .in2(controlled_buffer_1_out), .in3({16{1'b0}}),
    .out(multiplexer_3_out), .sel(PCMUX));
  Multiplexer #(.select(2), .width(16)) multiplexer_4 (
    .in0({16{1'b0}}), .in1(sext5_0_1_out_2), .in2(sext8_0_1_out_2), .in3(sext10_0_1_out_2),
    .out(multiplexer_4_out), .sel(ADDR2MUX));
  Register #(.width(16)) u_IR (.D(controlled_buffer_1_out), .en(LD_IR), .clk(CLK), .Q(IR), .clr(RST));
  Register #(.width(16)) u_MAR (.D(controlled_buffer_1_out), .en(LD_MAR), .clk(CLK), .Q(MAR), .clr(RST));
  Register #(.width(16)) u_MDR (.D(multiplexer_2_out), .en(LD_MDR), .clk(CLK), .Q(MDR), .clr(RST));
  assign controlled_buffer_1_out = GateMDR ? MDR : 16'bz;  // Controlled_Buffer controlled_buffer_2
  Register #(.width(16)) u_PC (.D(multiplexer_3_out), .en(LD_PC), .clk(CLK), .Q(PC), .clr(RST));
  Adder #(.width(16)) adder_1 (.a(multiplexer_4_out), .b(multiplexer_5_out), .out(adder_1_out));  // open: cin, cout
  Multiplexer #(.width(16)) multiplexer_5 (
    .in0(register_file_1_sr1_out), .in1(PC), .out(multiplexer_5_out), .sel(ADDR1MUX));
  LOGIC logic_1 (.I(controlled_buffer_1_out), .N(logic_1_n), .Z(logic_1_z), .P(logic_1_p));
  RAM #(.addrWidth(16), .dataWidth(16), .enables("line")) ram_1 (
    .addr(MAR), .we(R_W), .clk(CLK), .din(MDR), .dout(ram_1_dout));
  assign controlled_buffer_1_out = GatePC ? PC : 16'bz;  // Controlled_Buffer controlled_buffer_3
  DR_SEL dr_sel_1 (.DRMUX(DRMUX), .I(IR), .out_3(dr_sel_1_out_3));
  SR1_SEL sr1_sel_1 (.SR1MUX(SR1MUX), .I(IR), .O(sr1_sel_1_o));
  SEXT4_0 sext4_0_1 (.in_1(IR), .out_2(sext4_0_1_out_2));
  BIT_5 bit_5_1 (.I(IR), .O(bit_5_1_o));
  Register #(.width(1)) N (.D(logic_1_n), .en(LD_CC), .clk(CLK), .Q(N_q), .clr(RST));
  Register #(.width(1)) Z (.D(logic_1_z), .en(LD_CC), .clk(CLK), .Q(Z_q), .clr(RST));
  Register #(.width(1)) P (.D(logic_1_p), .en(LD_CC), .clk(CLK), .Q(P_q), .clr(RST));
  Adder #(.width(16)) adder_2 (.a(PC), .b(16'h1), .out(adder_2_out));  // open: cin, cout
  SR2_SEL sr2_sel_1 (.I(IR), .O(sr2_sel_1_o));
  BEN ben_1 (.P(P_q), .Z(Z_q), .LD_BEN(LD_BEN), .CLK(CLK), .R(RST), .N(N_q), .IR(IR), .O(ben_1_o));
  REGISTER_FILE register_file_1 (
    .I(controlled_buffer_1_out), .LDREG(LD_REG), .DR(dr_sel_1_out_3), .CLK(CLK), .R(RST), .SR1(sr1_sel_1_o),
    .SR2(sr2_sel_1_o), .R_0(R0), .R_1(R1), .R_2(R2), .R_3(R3), .SR1_OUT(register_file_1_sr1_out), .R_4(R4),
    .R_5(R5), .SR2_OUT(register_file_1_sr2_out), .R_6(R6), .R_7(R7));
  Multiplexer #(.width(16)) multiplexer_6 (
    .in0(register_file_1_sr2_out), .in1(sext4_0_1_out_2), .out(multiplexer_6_out), .sel(bit_5_1_o));
  ALU alu_1 (.A(register_file_1_sr1_out), .B(multiplexer_6_out), .OP(ALUK), .RES(alu_1_res));
  CONTROL_UNIT control_unit_1 (
    .IR(IR), .ACV(1'b0), .INT(1'b0), .PSR_15(1'b0), .BEN(ben_1_o), .CLK(CLK), .RST(RST), .MARMUX(MARMUX),
    .ALUK(ALUK), .MIO_EN(MIO_EN), .R_W(R_W), .LD_MAR(LD_MAR), .LD_MDR(LD_MDR), .LD_IR(LD_IR),
    .LD_BEN(LD_BEN), .LD_REG(LD_REG), .LD_CC(LD_CC), .LD_PC(LD_PC), .GatePC(GatePC), .GateMDR(GateMDR),
    .GateMARMUX(GateMARMUX), .PCMUX(PCMUX), .DRMUX(DRMUX), .SR1MUX(SR1MUX), .ADDR2MUX(ADDR2MUX),
    .GateALU(GateALU), .ADDR1MUX(ADDR1MUX));  // open: VectorMUX, Set_Priv, LD_Priv, LD_Vector, LD_ACV, GatePC1, GatePSR, GateSP, TableMUX, PSRMUX, LD_SavedSSP, LD_Priority, GateVector, SPMUX, LC_SavedUSP
  assign controlled_buffer_1_out = GateALU ? alu_1_res : 16'bz;  // Controlled_Buffer controlled_buffer_4
  Hex_Digit_Display hex_digit_display_1 (.value(PC[15:12]));  // open: dp
  Hex_Digit_Display hex_digit_display_2 (.value(IR[15:12]));  // open: dp
  Hex_Digit_Display hex_digit_display_3 (.value(R0[15:12]));  // open: dp
  Hex_Digit_Display hex_digit_display_4 (.value(R4[15:12]));  // open: dp
  Clock clock_1 (.out(CLK));
  Hex_Digit_Display hex_digit_display_5 (.value(PC[11:8]));  // open: dp
  Hex_Digit_Display hex_digit_display_6 (.value(PC[7:4]));  // open: dp
  Hex_Digit_Display hex_digit_display_7 (.value(IR[11:8]));  // open: dp
  Hex_Digit_Display hex_digit_display_8 (.value(IR[7:4]));  // open: dp
  Hex_Digit_Display hex_digit_display_9 (.value(R0[11:8]));  // open: dp
  Hex_Digit_Display hex_digit_display_10 (.value(R0[7:4]));  // open: dp
  Hex_Digit_Display hex_digit_display_11 (.value(R4[11:8]));  // open: dp
  Hex_Digit_Display hex_digit_display_12 (.value(R4[7:4]));  // open: dp
  Button u_RST (.out(RST));
  Hex_Digit_Display hex_digit_display_13 (.value(PC[3:0]));  // open: dp
  Hex_Digit_Display hex_digit_display_14 (.value(IR[3:0]));  // open: dp
  Hex_Digit_Display hex_digit_display_15 (.value(R0[3:0]));  // open: dp
  Hex_Digit_Display hex_digit_display_16 (.value(R4[3:0]));  // open: dp
  Hex_Digit_Display hex_digit_display_17 (.value(MAR[15:12]));  // open: dp
  Hex_Digit_Display hex_digit_display_18 (.value(MDR[15:12]));  // open: dp
  Hex_Digit_Display hex_digit_display_19 (.value(R1[15:12]));  // open: dp
  Hex_Digit_Display hex_digit_display_20 (.value(MAR[11:8]));  // open: dp
  Hex_Digit_Display hex_digit_display_21 (.value(MAR[7:4]));  // open: dp
  Hex_Digit_Display hex_digit_display_22 (.value(MDR[11:8]));  // open: dp
  Hex_Digit_Display hex_digit_display_23 (.value(R1[11:8]));  // open: dp
  Hex_Digit_Display hex_digit_display_24 (.value(R5[15:12]));  // open: dp
  Hex_Digit_Display hex_digit_display_25 (.value(R5[11:8]));  // open: dp
  Hex_Digit_Display hex_digit_display_26 (.value(MAR[3:0]));  // open: dp
  Hex_Digit_Display hex_digit_display_27 (.value(MDR[7:4]));  // open: dp
  Hex_Digit_Display hex_digit_display_28 (.value(MDR[3:0]));  // open: dp
  Hex_Digit_Display hex_digit_display_29 (.value(R1[7:4]));  // open: dp
  Hex_Digit_Display hex_digit_display_30 (.value(R1[3:0]));  // open: dp
  Hex_Digit_Display hex_digit_display_31 (.value(R5[7:4]));  // open: dp
  Hex_Digit_Display hex_digit_display_32 (.value(R5[3:0]));  // open: dp
  Hex_Digit_Display hex_digit_display_33 (.value(R2[15:12]));  // open: dp
  Hex_Digit_Display hex_digit_display_34 (.value(R2[11:8]));  // open: dp
  Hex_Digit_Display hex_digit_display_35 (.value(R6[15:12]));  // open: dp
  Hex_Digit_Display hex_digit_display_36 (.value(R6[11:8]));  // open: dp
  Hex_Digit_Display hex_digit_display_37 (.value(R2[7:4]));  // open: dp
  Hex_Digit_Display hex_digit_display_38 (.value(R2[3:0]));  // open: dp
  Hex_Digit_Display hex_digit_display_39 (.value(R6[7:4]));  // open: dp
  Hex_Digit_Display hex_digit_display_40 (.value(R6[3:0]));  // open: dp
  Hex_Digit_Display hex_digit_display_41 (.value(R3[15:12]));  // open: dp
  Hex_Digit_Display hex_digit_display_42 (.value(R3[11:8]));  // open: dp
  Hex_Digit_Display hex_digit_display_43 (.value(R7[15:12]));  // open: dp
  Hex_Digit_Display hex_digit_display_44 (.value(R7[11:8]));  // open: dp
  Hex_Digit_Display hex_digit_display_45 (.value(R3[7:4]));  // open: dp
  Hex_Digit_Display hex_digit_display_46 (.value(R3[3:0]));  // open: dp
  Hex_Digit_Display hex_digit_display_47 (.value(R7[7:4]));  // open: dp
  Hex_Digit_Display hex_digit_display_48 (.value(R7[3:0]));  // open: dp

  // Notes on the sheet:
  //   CLK
  //   PC
  //   IR
  //   R0
  //   R4
  //   MAR
  //   MDR
  //   R1
  //   R5
  //   REGISTER FILE
  //   R2
  //   R6
  //   R3
  //   R7
endmodule

module D_LATCH (
  input  D,
  input  WE,
  output Q
);

  wire nand_1_out, nand_2_out, nand_4_out;

  nand nand_1 (nand_1_out, D, WE);
  nand nand_2 (nand_2_out, WE, ~D);  // NAND_Gate
  nand nand_3 (Q, nand_1_out, nand_4_out);
  nand nand_4 (nand_4_out, Q, nand_2_out);
endmodule

module D_FLIP_FLOP (
  input  D,
  input  CLK,
  input  R,
  output Q
);

  wire and_1_out, d_latch_1_q, not_1_out, or_1_out;

  not not_1 (not_1_out, CLK);
  D_LATCH d_latch_1 (.WE(not_1_out), .D(D), .Q(d_latch_1_q));
  and and_1 (and_1_out, d_latch_1_q, ~R);  // AND_Gate
  or or_1 (or_1_out, CLK, R);
  D_LATCH d_latch_2 (.WE(or_1_out), .D(and_1_out), .Q(Q));
endmodule

module BYTE (
  input  [7:0] in_1,
  input  CLK,
  input  WE,
  input  R,
  output [7:0] out_5
);

  wire CLK_WE;

  and and_1 (CLK_WE, CLK, WE);
  D_FLIP_FLOP d_flip_flop_1 (.D(in_1[0]), .CLK(CLK_WE), .R(R), .Q(out_5[0]));
  D_FLIP_FLOP d_flip_flop_2 (.D(in_1[1]), .CLK(CLK_WE), .R(R), .Q(out_5[1]));
  D_FLIP_FLOP d_flip_flop_3 (.D(in_1[2]), .CLK(CLK_WE), .R(R), .Q(out_5[2]));
  D_FLIP_FLOP d_flip_flop_4 (.D(in_1[3]), .CLK(CLK_WE), .R(R), .Q(out_5[3]));
  D_FLIP_FLOP d_flip_flop_5 (.D(in_1[4]), .CLK(CLK_WE), .R(R), .Q(out_5[4]));
  D_FLIP_FLOP d_flip_flop_6 (.D(in_1[5]), .CLK(CLK_WE), .R(R), .Q(out_5[5]));
  D_FLIP_FLOP d_flip_flop_7 (.D(in_1[6]), .CLK(CLK_WE), .R(R), .Q(out_5[6]));
  D_FLIP_FLOP d_flip_flop_8 (.D(in_1[7]), .CLK(CLK_WE), .R(R), .Q(out_5[7]));
endmodule

module REG16 (
  input  [15:0] in_1,
  input  CLK,
  input  WE,
  input  R,
  output [15:0] out_5
);

  BYTE byte_1 (.in_1(in_1[7:0]), .CLK(CLK), .WE(WE), .R(R), .out_5(out_5[7:0]));
  BYTE byte_2 (.in_1(in_1[15:8]), .CLK(CLK), .WE(WE), .R(R), .out_5(out_5[15:8]));
endmodule

module REGISTER_FILE (
  input  [15:0] I,
  input  LDREG,
  input  [2:0] DR,
  input  CLK,
  input  R,
  input  [2:0] SR1,
  input  [2:0] SR2,
  output [15:0] R_0,
  output [15:0] R_1,
  output [15:0] R_2,
  output [15:0] R_3,
  output [15:0] SR1_OUT,
  output [15:0] R_4,
  output [15:0] R_5,
  output [15:0] SR2_OUT,
  output [15:0] R_6,
  output [15:0] R_7
);

  wire WE0, WE1, WE2, WE3, WE4, WE5, WE6, WE7;
  wire [15:0] D0, D1, D2, D3, D4, D5, D6, D7;

  Demultiplexer #(.select(3), .width(16)) demultiplexer_1 (
    .out0(D0), .out1(D1), .out2(D2), .out3(D3), .out4(D4), .out5(D5), .out6(D6), .out7(D7), .in(I), .sel(DR));
  Decoder #(.select(3)) decoder_1 (
    .out0(WE0), .out1(WE1), .out2(WE2), .out3(WE3), .out4(WE4), .out5(WE5), .out6(WE6), .out7(WE7), .sel(DR),
    .en(LDREG));
  Register #(.width(16)) R0 (.D(D0), .en(WE0), .clk(CLK), .Q(R_0), .clr(R));
  Register #(.width(16)) R2 (.D(D2), .en(WE2), .clk(CLK), .Q(R_2), .clr(R));
  Register #(.width(16)) R4 (.D(D4), .en(WE4), .clk(CLK), .Q(R_4), .clr(R));
  Register #(.width(16)) R6 (.D(D6), .en(WE6), .clk(CLK), .Q(R_6), .clr(R));
  Register #(.width(16)) R1 (.D(D1), .en(WE1), .clk(CLK), .Q(R_1), .clr(R));
  Register #(.width(16)) R3 (.D(D3), .en(WE3), .clk(CLK), .Q(R_3), .clr(R));
  Register #(.width(16)) R5 (.D(D5), .en(WE5), .clk(CLK), .Q(R_5), .clr(R));
  Register #(.width(16)) R7 (.D(D7), .en(WE7), .clk(CLK), .Q(R_7), .clr(R));
  Multiplexer #(.select(3), .width(16)) multiplexer_1 (
    .in0(R_0), .in1(R_1), .in2(R_2), .in3(R_3), .in4(R_4), .in5(R_5), .in6(R_6), .in7(R_7), .out(SR1_OUT),
    .sel(SR1));
  Multiplexer #(.select(3), .width(16)) multiplexer_2 (
    .in0(R_0), .in1(R_1), .in2(R_2), .in3(R_3), .in4(R_4), .in5(R_5), .in6(R_6), .in7(R_7), .out(SR2_OUT),
    .sel(SR2));

  // Other names for the same wires on the sheet: Q0[15:0] = R_0; Q1[15:0] = R_1; Q2[15:0] = R_2; Q3[15:0] = R_3;
  //   Q4[15:0] = R_4; Q5[15:0] = R_5; Q6[15:0] = R_6; Q7[15:0] = R_7; RST = R
endmodule

module ALU (
  input  [15:0] A,
  input  [15:0] B,
  input  [1:0] OP,
  output [15:0] RES
);

  wire [15:0] adder_1_out, and_1_out, not_1_out;

  Adder #(.width(16)) adder_1 (.a(A), .b(B), .out(adder_1_out));  // open: cin, cout
  assign and_1_out = A & B;  // AND_Gate and_1, 16 bits wide
  assign not_1_out = ~A;  // NOT_Gate not_1, 16 bits wide
  Multiplexer #(.select(2), .width(16)) multiplexer_1 (
    .in0(adder_1_out), .in1(and_1_out), .in2(not_1_out), .out(RES), .sel(OP));  // open: in3
endmodule

module CONTROL_UNIT (
  input  [15:0] IR,
  input  ACV,
  input  INT,
  input  PSR_15,
  input  BEN,
  input  CLK,
  input  RST,
  output MARMUX,
  output [1:0] VectorMUX,
  output [1:0] ALUK,
  output MIO_EN,
  output R_W,
  output Set_Priv,
  output LD_MAR,
  output LD_MDR,
  output LD_IR,
  output LD_BEN,
  output LD_REG,
  output LD_CC,
  output LD_PC,
  output LD_Priv,
  output LD_Vector,
  output LD_ACV,
  output GatePC,
  output GateMDR,
  output GateMARMUX,
  output GatePC1,
  output GatePSR,
  output GateSP,
  output [1:0] PCMUX,
  output [1:0] DRMUX,
  output [1:0] SR1MUX,
  output [1:0] ADDR2MUX,
  output TableMUX,
  output PSRMUX,
  output LD_SavedSSP,
  output LD_Priority,
  output GateALU,
  output GateVector,
  output ADDR1MUX,
  output [1:0] SPMUX,
  output LC_SavedUSP
);

  wire and_1_out, and_2_out, and_3_out, and_4_out, and_5_out, and_6_out, IRD, or_1_out;
  wire [2:0] COND;
  wire [5:0] J, multiplexer_1_out, multiplexer_2_out, or_7_out, register_1_q;
  wire [51:0] rom_1_data;

  Multiplexer #(.width(6)) multiplexer_1 (.in0(multiplexer_2_out), .in1(6'b010010), .out(multiplexer_1_out), .sel(RST));
  or or_1 (or_1_out, RST, CLK);
  Register #(.trigger("high"), .width(6)) register_1 (
    .D(multiplexer_1_out), .en(1'b1), .clk(or_1_out), .Q(register_1_q));  // open: clr
  ROM #(.addrWidth(6), .dataWidth(52)) rom_1 (.addr(register_1_q), .data(rom_1_data));
  Multiplexer #(.width(6)) multiplexer_2 (.in0(or_7_out), .in1({2'b00, IR[15:12]}), .out(multiplexer_2_out), .sel(IRD));
  and and_1 (and_1_out, COND[2], COND[1], ~COND[0], ACV);  // AND_Gate
  or or_2 (or_7_out[5], J[5], and_1_out);
  and and_2 (and_2_out, COND[2], ~COND[1], COND[0], INT);  // AND_Gate
  or or_3 (or_7_out[4], J[4], and_2_out);
  and and_3 (and_3_out, COND[2], ~COND[1], ~COND[0], PSR_15);  // AND_Gate
  or or_4 (or_7_out[3], J[3], and_3_out);
  Register #(.width(52)) register_2 (
    .D(rom_1_data), .en(1'b1), .clk(CLK),
    .Q({IRD, COND, J, LD_MAR, LD_MDR, LD_IR, LD_BEN, LD_REG, LD_CC, LD_PC, LD_Priv, LD_SavedSSP, LC_SavedUSP, LD_Vector, LD_Priority, LD_ACV, GatePC, GateMDR, GateALU, GateMARMUX, GateVector, GatePC1, GatePSR, GateSP, PCMUX, DRMUX, SR1MUX, ADDR1MUX, ADDR2MUX, SPMUX, MARMUX, TableMUX, VectorMUX, PSRMUX, ALUK, MIO_EN, R_W, Set_Priv}),
    .clr(RST));
  and and_4 (and_4_out, ~COND[2], COND[1], ~COND[0], BEN);  // AND_Gate
  or or_5 (or_7_out[1], J[1], and_5_out);
  or or_6 (or_7_out[2], J[2], and_4_out);
  and and_5 (and_5_out, ~COND[2], ~COND[1], COND[0], 1'b1);  // AND_Gate
  and and_6 (and_6_out, ~COND[2], COND[1], COND[0], IR[11]);  // AND_Gate
  or or_7 (or_7_out[0], J[0], and_6_out);

  // Notes on the sheet:
  //   contents of rom_1 (hex, n*v repeats v):
  //   2480000000000 483004000000 8e0022006200 5e0022006200 0 483004000008 8e0022001200 5e0022001200 0
  //   483004000010 460022006200 4e0022006200 0 0 482002006200 0 1400000000002 6600000000000 5860830000000
  //   6740000000000 0 0 0 6410002008200 1610000000004 1650000000004 8e0008000000 483008000000
  //   1710000000004 17d0000000004 808008000000 5e0028000000 8004000000000 6700000000000 0 6640000000000
endmodule

module LOGIC (
  input  [15:0] I,
  output N,
  output Z,
  output P
);

  and and_1 (Z, ~I[15], ~I[14], ~I[13], ~I[12], ~I[11], ~I[10], ~I[9], ~I[8], ~I[7], ~I[6], ~I[5], ~I[4], ~I[3], ~I[2], ~I[1], ~I[0]);  // AND_Gate
  and and_2 (P, ~Z, ~I[15]);  // AND_Gate

  assign N = I[15];
endmodule

module SEXT4_0 (
  input  [15:0] in_1,
  output [15:0] out_2
);


  assign out_2 = {{12{in_1[4]}}, in_1[3:0]};
endmodule

module BIT_5 (
  input  [15:0] I,
  output O
);


  assign O = I[5];
endmodule

module SEXT5_0 (
  input  [15:0] in_1,
  output [15:0] out_2
);


  assign out_2 = {{11{in_1[5]}}, in_1[4:0]};
endmodule

module SEXT8_0 (
  input  [15:0] in_1,
  output [15:0] out_2
);


  assign out_2 = {{8{in_1[8]}}, in_1[7:0]};
endmodule

module SEXT10_0 (
  input  [15:0] in_1,
  output [15:0] out_2
);


  assign out_2 = {{6{in_1[10]}}, in_1[9:0]};
endmodule

module ZEXT7_0 (
  input  [15:0] in_1,
  output [15:0] out_2
);


  assign out_2 = {{8{1'b0}}, in_1[7:0]};
endmodule

module BEN (
  input  P,
  input  Z,
  input  LD_BEN,
  input  CLK,
  input  R,
  input  N,
  input  [15:0] IR,
  output O
);

  wire and_1_out, and_2_out, and_3_out, or_1_out;

  and and_1 (and_1_out, IR[9], P);
  and and_2 (and_2_out, IR[10], Z);
  and and_3 (and_3_out, IR[11], N);
  or or_1 (or_1_out, and_1_out, and_2_out, and_3_out);
  Register #(.width(1)) register_1 (.D(or_1_out), .en(LD_BEN), .clk(CLK), .Q(O), .clr(R));
endmodule

module DR_SEL (
  input  [1:0] DRMUX,
  input  [15:0] I,
  output [2:0] out_3
);

  Multiplexer #(.select(2), .width(3)) multiplexer_1 (
    .in0(I[11:9]), .in1(3'b110), .in2(3'b111), .in3(3'b000), .out(out_3), .sel(DRMUX));
endmodule

module SR1_SEL (
  input  [1:0] SR1MUX,
  input  [15:0] I,
  output [2:0] O
);

  Multiplexer #(.select(2), .width(3)) multiplexer_1 (
    .in0(I[8:6]), .in1(I[11:9]), .in2(3'b110), .in3(3'b000), .out(O), .sel(SR1MUX));
endmodule

module SR2_SEL (
  input  [15:0] I,
  output [2:0] O
);


  assign O = I[2:0];
endmodule
